# Fritzing sketch Arduino Nano 2 (saved by Fritzing 1.0.1rc)
stripboards: 3

parts:
  M1 = Arduino NANO RP2040 CONNECT with headers  # not connected
  Part1 = Arduino Nano (Rev3.0)
  R1 = Resistor Mini [tolerance=±5% resistance=3.3k package=THT]
  R2 = Resistor Mini [tolerance=±5% resistance=3.3k package=THT]
  R3 = Resistor Mini [tolerance=±5% resistance=3.3k package=THT]
  R4 = Resistor Mini [tolerance=±5% resistance=3.3k package=THT]
  R6 = Resistor Mini [tolerance=±5% resistance=3.3k package=THT]
  R7 = Resistor Mini [tolerance=±5% resistance=3.3k package=THT]
  R8 = Resistor Mini [tolerance=±5% resistance=3.3k package=THT]
  R9 = Resistor Mini [tolerance=±5% resistance=3.3k package=THT]
  R10 = Resistor Mini [tolerance=±5% resistance=3.3k package=THT]
  R11 = Resistor Mini [tolerance=±5% resistance=3.3k package=THT]
  R12 = Resistor Mini [tolerance=±5% resistance=3.3k package=THT]
  R14 = Resistor Mini [tolerance=±5% resistance=3.3k package=THT]
  R15 = Resistor Mini [tolerance=±5% resistance=3.3k package=THT]
  R16 = Resistor Mini [tolerance=±5% resistance=3.3k package=THT]
  R17 = Resistor Mini [tolerance=±5% resistance=3.3k package=THT]
  R18 = Resistor Mini [tolerance=±5% resistance=3.3k package=THT]
  R20 = Rotary Potentiometer (Small) [maximum_resistance=10kΩ knob_status=50% power=0.5W package=THT]
  R21 = Rotary Potentiometer (Small) [maximum_resistance=10kΩ knob_status=50% power=0.5W package=THT]
  R22 = Rotary Potentiometer (Small) [maximum_resistance=10kΩ knob_status=50% power=0.5W package=THT]

nets:
  N1: Part1.5V, R1.Pin_0, R2.Pin_0, R3.Pin_1, R4.Pin_1
  N2: R6.Pin_1, R7.Pin_0, R8.Pin_1
  N3: R9.Pin_1, R10.Pin_0, R11.Pin_0
  N4: R12.Pin_0, R14.Pin_0, R15.Pin_0, R16.Pin_1, R17.Pin_1, R18.Pin_1
  N5: R12.Pin_1, R21.leg1
  N6: R14.Pin_1, R20.leg1
  N7: R15.Pin_1, R21.leg2
  N8: R16.Pin_0, R20.leg2
  N9: R17.Pin_0, R22.leg1
  N10: R18.Pin_0, R22.leg2
  N11: R20.wiper, R21.wiper, R22.wiper

custom parts:
  Resistor Mini: A generic resistor (0.25W)
