# Fritzing sketch Arduino Nano 4 (saved by Fritzing 1.0.1rc)
stripboards: 1

parts:
  R12 = Resistor Mini [tolerance=±5% resistance=3.3k package=THT]
  R14 = Resistor Mini [tolerance=±5% resistance=3.3k package=THT]
  R15 = Resistor Mini [tolerance=±5% resistance=3.3k package=THT]
  R16 = Resistor Mini [tolerance=±5% resistance=3.3k package=THT]
  R17 = Resistor Mini [tolerance=±5% resistance=3.3k package=THT]
  R18 = Resistor Mini [tolerance=±5% resistance=3.3k package=THT]
  Pencil = Rotary Potentiometer (Small) [maximum_resistance=10kΩ knob_status=50% power=0.5W package=THT]
  Pencil_2 = Rotary Potentiometer (Small) [maximum_resistance=10kΩ knob_status=50% power=0.5W package=THT]
  Pencil_3 = Rotary Potentiometer (Small) [maximum_resistance=10kΩ knob_status=50% power=0.5W package=THT]
  Arduino_Nano = Arduino Nano (Rev3.0)

nets:
  5V: R12.Pin_0, R14.Pin_0, R15.Pin_0, R16.Pin_1, R17.Pin_1, R18.Pin_1, Arduino_Nano.5V
  N1: R12.Pin_1, Pencil_2.leg1, Arduino_Nano.A6
  N2: R14.Pin_1, Pencil.leg1, Arduino_Nano.A4
  N3: R15.Pin_1, Pencil_2.leg2, Arduino_Nano.A5
  N4: R16.Pin_0, Pencil.leg2, Arduino_Nano.A3
  N5: R17.Pin_0, Pencil_3.leg1, Arduino_Nano.A2
  N6: R18.Pin_0, Pencil_3.leg2, Arduino_Nano.A1
  GND: Pencil.wiper, Pencil_2.wiper, Pencil_3.wiper, Arduino_Nano.GND

custom parts:
  Resistor Mini: A generic resistor (0.25W)
