# Fritzing sketch Arduino Nano (saved by Fritzing 1.0.1rc)
stripboards: 2

parts:
  Part1 = Arduino Nano (Rev3.0)
  R1 = Rotary Potentiometer (Small) [maximum_resistance=100kΩ knob_status=50% power=0.5W package=THT]  # not connected
  R2 = Rotary Potentiometer (Small) [maximum_resistance=100kΩ knob_status=50% power=0.5W package=THT]
  R3 = Rotary Potentiometer (Small) [maximum_resistance=100kΩ knob_status=50% power=0.5W package=THT]  # not connected
  R4 = Resistor [tolerance=±5% power=0.25W resistance=3.3k package=THT]  # not connected
  R6 = Resistor [tolerance=±5% power=0.25W resistance=3.3k package=THT]
  R7 = Resistor [tolerance=±5% power=0.25W resistance=3.3k package=THT]
  R8 = Resistor [tolerance=±5% power=0.25W resistance=3.3k package=THT]
  R9 = Resistor [tolerance=±5% power=0.25W resistance=3.3k package=THT]  # not connected
  R10 = Resistor [tolerance=±5% power=0.25W resistance=3.3k package=THT]
  R11 = Resistor [tolerance=±5% power=0.25W resistance=3.3k package=THT]  # not connected
  R12 = Resistor [tolerance=±5% power=0.25W resistance=3.3k package=THT]  # not connected

nets:
  N1: Part1.5V, R6.Pin_0, R7.Pin_0, R8.Pin_0, R10.Pin_0
  N2: R2.leg1, R6.Pin_1
  N3: R2.leg2, R10.Pin_1
  N4: R7.Pin_1, R8.Pin_1
