# Fritzing sketch pencil-measurement (saved by Fritzing 1.0.1rc)
breadboards: 1

parts:
  R4 = Rotary Potentiometer (Small) [maximum_resistance=1kΩ knob_status=50% power=0.5W package=THT]
  R2 = Resistor [tolerance=±5% power=0.25W resistance=1k package=THT]
  Part1 = Arduino Uno (Rev3)
  R1 = Resistor [tolerance=±5% power=0.25W resistance=1k package=THT]
  R3 = Rotary Potentiometer (Small) [maximum_resistance=50Ω knob_status=50% power=0.5W package=THT]

nets:
  N1: R4.leg1, R2.Pin_1, Part1.A1
  N2: R4.wiper, Part1.5V, R3.wiper
  N3: R2.Pin_0, Part1.GND, R1.Pin_0
  N4: Part1.A0, R1.Pin_1, R3.leg1
